# Fritzing sketch gyro_328p_6050_2021 (saved by Fritzing 0.9.9b)
circuit board: 3.09999cm x 6.50001cm
breadboards: 1

parts:
  LED3 = LED - 3mm [color="Green (560nm)" current=0.030 package="3 mm [THT]"]
  J1 = female pin header, 3 pins [form="♀ (female)"]
  R2 = Resistor [tolerance=±5% resistance=470 power=0.25 package=THT]
  LED1 = LED - 3mm [color="Green (560nm)" current=0.030 package="3 mm [THT]"]
  R3 = Resistor [tolerance=±5% resistance=470 power=0.25 package=THT]
  R1 = Resistor [tolerance=±5% resistance=470 power=0.25 package=THT]
  ATMEGA328P = IC, DIP package, 28 pins [chip_label=328p]
  Y1 = Resonator [frequency="16 Mhz" package=THT]
  MCP4726 = IC, DIP package, 6 pins [chip_label=DAC]
  C104 = Ceramic Capacitor [capacitance=10nF voltage=10V package="100 mil [THT, multilayer]"]
  MPU6050 = MPU-6050 4pin [form="♀ (female)" package=THT]
  C103 = Ceramic Capacitor [capacitance=100nF voltage=10V package="100 mil [THT, multilayer]"]
  SW = Pushbutton [package="[THT]"]
  J2 = male pin header, 6 pins [form="♂ (male)"]
  R10k = Resistor [tolerance=±5% resistance=10k power=0.25 package=THT]
  OLED = OLED I2C 128x32 [package="DIP (Dual Inline) [THT]"]
  LED2 = LED - 3mm [color="Green (560nm)" current=0.030 package="3 mm [THT]"]

nets:
  N1: LED3.cathode, R3.Pin_1
  N2: LED3.anode, ATMEGA328P.pin19
  N3: J1.pin1, MCP4726.pin1
  5V: J1.pin2, ATMEGA328P.pin7, ATMEGA328P.pin20, ATMEGA328P.pin21, MCP4726.pin3, MCP4726.pin6, C104.1, MPU6050.pin1, J2.pin3, R10k.Pin_1, OLED.VCC
  GND: J1.pin3, R2.Pin_0, R3.Pin_0, R1.Pin_0, ATMEGA328P.pin8, ATMEGA328P.pin22, Y1.GND, MCP4726.pin2, C104.0, MPU6050.pin2, SW.Pin_3, SW.Pin_4, J2.pin1, J2.pin2, OLED.GND
  N4: R2.Pin_1, LED2.cathode
  N5: LED1.cathode, R1.Pin_1
  N6: LED1.anode, ATMEGA328P.pin17
  N7: ATMEGA328P.pin1, C103.0, R10k.Pin_0
  N8: ATMEGA328P.pin2, J2.pin4
  N9: ATMEGA328P.pin3, J2.pin5
  N10: ATMEGA328P.pin9, Y1.0
  N11: ATMEGA328P.pin10, Y1.pin_1
  N12: ATMEGA328P.pin18, LED2.anode
  N13: ATMEGA328P.pin26, SW.Pin_1, SW.Pin_2
  N14: ATMEGA328P.pin27, MCP4726.pin4, MPU6050.pin4, OLED.SDA
  N15: ATMEGA328P.pin28, MCP4726.pin5, MPU6050.pin3, OLED.SCL
  N16: C103.1, J2.pin6

notes:
  2021-12
  Analog Gyro
  @ohguma
  DTR  TX   RX  5V   GND GND
  D10 D9
  D8  D7
  D4  D3  D2
  A2   A1   A0   5V
  SDA  SCL  5V  GND
  GND 5V  OUT
  OUT 5V  GND
  5V  GND  SCL SDA
  GND GND   5V  RX   TX  DTR
  D7  D8
  D9 D10
  5V   A0   A1   A2
  VDD VSS VOUT
  VREF SCL SDA
  D2  D3  D4
  D5  D6
  D6 D5
  GND

custom parts:
  MPU-6050 4pin: Placa GY-521 basada en conjunto de acelerómetro+giroscopios MPU-6050 RafaG
